// Logisim project 1bit_CPU.circ as structural Verilog: 2 circuits, main circuit One_Bit_CPU
module One_Bit_CPU (
  input  Reset,
  input  Clock,
  input  DataIn,
  input  [7:0] InstructionIn,
  output DataOut,
  output Write,
  output [10:0] DataAddress,
  output [11:0] InstructionAddress
);

  wire Accumulator_q, bitselector_1_out, Clk2, FetchNext_qn;
  wire [0:0] InstructionRegister_q_2;
  wire [2:0] InstructionRegister_q, StackPointer_q;
  wire [3:0] and_1_out;
  wire [6:6] FetchNext_q;
  wire [11:0] InstructionRegister_q_3, multiplexer_1_out, ProgramStack_dout;
  wire [16:0] Microcode_data;

  not not_1 (Clk2, Clock);
  ROM #(.addrWidth(7), .dataWidth(17)) Microcode (
    .addr({FetchNext_q[6], InstructionRegister_q_3[1:0], InstructionRegister_q_2[0], InstructionRegister_q}),
    .data(Microcode_data));
  Counter #(.max('h7), .width(3)) StackPointer (
    .clr(Reset), .load(Microcode_data[15]), .up(Microcode_data[16]), .count(1'b1), .clk(Clock),
    .Q(StackPointer_q));  // open: D, carry
  // Probe on Microcode_data
  RAM #(.addrWidth(3), .dataWidth(12)) ProgramStack (
    .addr(StackPointer_q), .we(Microcode_data[13]), .oe(Microcode_data[14]), .din(InstructionAddress),
    .dout(ProgramStack_dout));  // open: clk
  and and_1 (and_1_out[0], and_1_out[3], Accumulator_q);
  or or_1 (and_1_out[1], and_1_out[3], Accumulator_q);
  not not_2 (and_1_out[2], Accumulator_q);
  T_Flip_Flop FetchNext (
    .T(Microcode_data[12]), .clk(Clock), .Q(FetchNext_q[6]), .Qn(FetchNext_qn), .reset(Reset));  // open: preset
  Register ExtraByte (
    .D(InstructionIn), .en(FetchNext_q[6]), .clk(Clock), .Q(InstructionRegister_q_3[11:4]), .clr(Reset));
  Register InstructionRegister (
    .D(InstructionIn), .en(FetchNext_qn), .clk(Clock),
    .Q({InstructionRegister_q_3[3:0], InstructionRegister_q_2[0], InstructionRegister_q}), .clr(Reset));
  Register #(.width(1)) Accumulator (
    .D(bitselector_1_out), .en(Microcode_data[3]), .clk(Clock), .Q(Accumulator_q), .clr(Reset));
  BitSelector #(.width(7)) bitselector_1 (
    .in({2'b01, DataIn, and_1_out}), .out(bitselector_1_out), .sel(Microcode_data[2:0]));
  Multiplexer #(.width(12)) multiplexer_1 (
    .in0(InstructionRegister_q_3), .in1(ProgramStack_dout), .out(multiplexer_1_out), .sel(Microcode_data[11]));
  RAM #(.addrWidth(5), .dataWidth(1)) Registers (
    .addr({InstructionRegister_q_3[3:0], InstructionRegister_q_2[0]}), .we(Microcode_data[4]), .oe(1'b1),
    .clk(Clk2), .din(Accumulator_q), .dout(and_1_out[3]));
  Counter #(.max('hfff), .width(12)) ProgramCounter (
    .clr(Reset), .load(Microcode_data[9]), .up(Microcode_data[10]), .count(1'b1), .clk(Clk2),
    .D(multiplexer_1_out), .Q(InstructionAddress));  // open: carry
  Counter #(.max('h7ff), .width(11)) AddressLatch_IncDec (
    .clr(Reset), .load(Microcode_data[7]), .up(Microcode_data[8]), .count(1'b1), .clk(Clk2),
    .D(InstructionRegister_q_3[11:1]), .Q(DataAddress));  // open: carry
  Register #(.width(1)) DataOutLatch (.D(Accumulator_q), .en(Microcode_data[5]), .clk(Clk2), .Q(DataOut), .clr(Reset));
  Register #(.width(1)) WriteLatch (
    .D(InstructionRegister_q_3[0]), .en(Microcode_data[6]), .clk(Clk2), .Q(Write), .clr(Reset));

  // Other names for the same wires on the sheet: Clk1 = Clock; Rst = Reset

  // Notes on the sheet:
  //   contents of Microcode (hex, n*v repeats v):
  //   408 0 408 0 408 0 408 0 408 0 408 0 408 0 408 0 40c 0 40c 0 40c 0 40c 0 40c 0 40c 0 40c 0 40c 0 40e
  //   0 40e 0 40e 0 40e 0 40e 0 40e 0 40e 0 40e 0 410 0 410 0 410 0 410 0 410 0 410 0 410 0 410 0 40a 0 0
  //   0 40b 0 40d
endmodule

module CPU_and_ProgramRom (
);

  wire MasterClock_out, por_1_out;
  wire [7:0] ProgramROM_data;
  wire [11:0] one_bit_cpu_1_instructionaddress;

  Clock #(.highDuration(3), .lowDuration(3)) MasterClock (.out(MasterClock_out));
  POR por_1 (.out(por_1_out));
  ROM #(.addrWidth(12)) ProgramROM (.addr(one_bit_cpu_1_instructionaddress), .data(ProgramROM_data));
  One_Bit_CPU one_bit_cpu_1 (
    .Reset(por_1_out), .Clock(MasterClock_out), .InstructionIn(ProgramROM_data),
    .InstructionAddress(one_bit_cpu_1_instructionaddress));  // open: DataIn, DataOut, Write, DataAddress

  // Notes on the sheet:
  //   contents of ProgramROM (hex, n*v repeats v):
  //   89 60 21 61
endmodule
